# Fritzing sketch 3 HC SR 04 (saved by Fritzing 0.9.3b)

parts:
  Part1 = Arduino Leonardo (Rev3b)
  HC-SR04_Sensor_1 = HC-SR04 Ultrasonic Distance Sensor
  HC-SR04_Sensor_2 = HC-SR04 Ultrasonic Distance Sensor
  HC-SR04_Sensor_3 = HC-SR04 Ultrasonic Distance Sensor

nets:
  N1: Part1.D2/SDA, HC-SR04_Sensor_3.TRIG
  N2: Part1.D3_PWM/SCL, HC-SR04_Sensor_3.ECHO
  N3: Part1.D4/A6, HC-SR04_Sensor_2.VCC, HC-SR04_Sensor_2.TRIG
  N4: Part1.D5_PWM, HC-SR04_Sensor_2.ECHO
  5V: Part1.D7, Part1.5V, HC-SR04_Sensor_1.VCC, HC-SR04_Sensor_1.TRIG
  GND: Part1.GND, HC-SR04_Sensor_3.GND
  N5: Part1.D8/A8, HC-SR04_Sensor_1.ECHO
