# Fritzing sketch noi day bluetooth (saved by Fritzing 0.9.3b)

parts:
  Part3 = Arduino Uno (Rev3) - ICSP
  Part4 = HC-05 [part_number=HC-05 package="breakout board"]

nets:
  N1: Part3.A2, Part4.TXD
  N2: Part3.A3, Part4.RXD
  5V: Part3.5V, Part4.VCC
  GND: Part3.GND, Part4.GND

custom parts:
  HC-05: A commonly available HC-05 Bluetooth breakout board.
