# Fritzing sketch so do mach toan bo (saved by Fritzing 0.9.3b)

parts:
  Part2 = Arduino Uno (Rev3) - ICSP
  L298N2 = L298N DC motor driver
  M5 = Getriebemotor
  M6 = Getriebemotor
  M7 = Getriebemotor
  M8 = Getriebemotor
  JACK2 = 2.1mm Barrel Jack with Terminal Block  # not connected
  HC-SR04_Sensor_1 = HC-SR04 Ultrasonic Distance Sensor
  HC-SR04_Sensor_2 = HC-SR04 Ultrasonic Distance Sensor
  HC-SR04_Sensor_3 = HC-SR04 Ultrasonic Distance Sensor
  Part3 = HC-05 [part_number=HC-05 package="breakout board"]
  ZS-042_RTC1 = ZS-042 RTC Module
  S1 = Pushbutton [package="[THT]"]
  SPKR1 = Loudspeaker

nets:
  N1: Part2.A0, S1.Pin_1
  N2: Part2.A1, SPKR1.pin2
  N3: Part2.A2, Part3.TXD
  N4: Part2.A3, Part3.RXD
  N5: Part2.A4/SDA, ZS-042_RTC1.SDA
  N6: Part2.A5/SCL, ZS-042_RTC1.SCL
  N7: Part2.D8, HC-SR04_Sensor_3.ECHO
  N8: Part2.D9_PWM, L298N2.ENB
  N9: Part2.D10_PWM/SS, L298N2.ENA
  N10: Part2.D11_PWM/MOSI, L298N2.IN1
  N11: Part2.D12/MISO, L298N2.IN2
  N12: Part2.D13/SCK, L298N2.IN3
  GND: Part2.GND, L298N2.GND, S1.Pin_3, SPKR1.pin1
  N13: Part2.D2, HC-SR04_Sensor_1.TRIG
  N14: Part2.D3_PWM, HC-SR04_Sensor_1.ECHO
  N15: Part2.D4, HC-SR04_Sensor_2.ECHO
  N16: Part2.D5_PWM, HC-SR04_Sensor_2.TRIG
  N17: Part2.D6_PWM, L298N2.IN4
  N18: Part2.D7, HC-SR04_Sensor_3.TRIG
  N19: L298N2.OUT1, M7.pin_2, M8.pin_2
  N20: L298N2.OUT2, M7.pin_1, M8.pin_1
  N21: L298N2.OUT3, M5.pin_1, M6.pin_1
  N22: L298N2.OUT4, M5.pin_2, M6.pin_2

custom parts:
  L298N DC motor driver: 2x DC motor driver with 78M05 positive voltage regulator (7..35 V) L298N: max 46 V, 2 A Set 5 V Enable jumper to enable 5 V regultor (needed for the L298N) and +5 V output at screw terminal or supply external +5 V at screw terminal Set ENA and/or ENB to +5 V to enable motor permanently or supply ENA and/or ENB with PWM signal IN1 and IN2 set rotation directory for motor A (OUT1/OUT2) IN2 and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
  HC-05: A commonly available HC-05 Bluetooth breakout board.
