# Fritzing sketch Lắp cảm biến với arduino (saved by Fritzing 0.9.3b)

parts:
  Part2 = Arduino BT
  LM_393 = LM393 LDR breakout [part_number=100027]

nets:
  GND: Part2.GND, LM_393.GND
  N1: Part2.A0, LM_393.AO
  N2: Part2.PWM_D3, LM_393.DO
  5V: Part2.5V, LM_393.VCC
