# Fritzing sketch Tongquan (saved by Fritzing 0.9.3b)
breadboards: 1

parts:
  e-radionica_com1 = LM393 LDR breakout [part_number=100027]
  e-radionica_com2 = LM393 LDR breakout [part_number=100027]
  LED1 = smd LED [color="Red (633nm)" package="1206 [SMD]"]
  LED2 = smd LED [color="Red (633nm)" package="1206 [SMD]"]
  S1 = Round Pushbutton
  R1 = Resistor [tolerance=±5% resistance=220 package=THT]
  R2 = Resistor [tolerance=±5% resistance=220 package=THT]
  Part1 = Arduino BT
  Part2 = LCD1602-I2C

nets:
  VCC: e-radionica_com1.VCC, e-radionica_com2.VCC, Part1.5V, Part2.VCC
  GND: e-radionica_com1.GND, e-radionica_com2.GND, LED1.cathode, LED2.cathode, S1.leg0, Part1.GND, Part2.GND
  N1: e-radionica_com1.AO, Part1.A2
  N2: e-radionica_com2.AO, Part1.A1
  N3: LED1.anode, R1.Pin_0
  N4: LED2.anode, R2.Pin_0
  N5: S1.leg1, Part1.D2
  N6: R1.Pin_1, Part1.PWM_D9
  N7: R2.Pin_1, Part1.D8
  N8: Part1.A4/SDA, Part2.SCL
  N9: Part1.A5/SCL, Part2.SDA

custom parts:
  LCD1602-I2C: A standard character display, usually with 2x16 characters. Comes in many colors with LCM1602 IIC attached.
