# Fritzing sketch Tong_quan (saved by Fritzing 0.9.3b)
breadboards: 1

parts:
  e-radionica_com1 = prefix100027 [part_number=100027]
  e-radionica_com2 = prefix100027 [part_number=100027]
  LED1 = smd LED [color="Red (633nm)" package="1206 [SMD]"]
  R1 = Resistor [tolerance=±5% resistance=220 package=THT]
  Part1 = Arduino BT
  Part2 = LCD1602-I2C_
  S1 = Pushbutton [package="[SMD]"]

nets:
  N1: e-radionica_com1.connector0, e-radionica_com2.connector0, Part1.5V, Part2.connector1
  N2: e-radionica_com1.connector2, e-radionica_com2.connector2, LED1.cathode, Part1.RESET_WT11/D7, Part1.GND, Part2.connector0, S1.Pin_3, S1.Pin_4
  N3: e-radionica_com1.connector3, Part1.A0
  N4: e-radionica_com1.connector4, Part1.PWM_D3
  N5: e-radionica_com2.connector4, Part1.D2
  N6: LED1.anode, R1.Pin_0
  N7: R1.Pin_1, Part1.MOSI/PWM_D11
  N8: Part1.A4, Part2.connector2
  N9: Part1.A5, Part2.connector3
  N10: S1.Pin_1, S1.Pin_2
